# Fritzing sketch AX-12_Bluetooth_MasterSlave (saved by Fritzing 0.9.3b)
breadboards: 1

parts:
  Part1 = Arduino Uno (Rev3)
  Part2 = Arduino Uno (Rev3)
  Part3 = Bluetooth HC-05 Macho
  Part4 = Bluetooth HC-05 Macho
  IC1 = IC, DIP package, 20 pins [chip_label=SN74LS241N]
  IC2 = IC, DIP package, 20 pins [chip_label=SN74LS241N]
  Power_plug1 = Power plug
  S1 = Toggle Switch [package=THT]
  R1 = Resistor [tolerance=±5% resistance=220 package=THT]
  JP1 = Header 3 [package=molex-1x3_lock]
  JP2 = Header 3 [package=molex-1x3_lock]
  S2 = Toggle Switch [package=THT]
  R2 = Resistor [tolerance=±5% resistance=220 package=THT]

nets:
  N1: Part1.D10_PWM/SS, Part3.TXD
  N2: Part1.D11_PWM/MOSI, Part3.RXD
  GND: Part1.GND, Part2.GND, Part3.GND, Part4.GND, IC1.pin10, IC2.pin10, Power_plug1.GND, JP1.3, JP2.3
  N3: Part1.D0/RX, S1.L1
  N4: Part1.D1/TX, IC1.pin17
  N5: Part1.D2, IC1.pin1, IC1.pin19
  5V: Part1.5V, Part3.VCC, IC1.pin20, R1.Pin_0
  VIN: Part1.VIN, Part2.VIN, Power_plug1.VCC, JP1.2, JP2.2
  N6: Part2.D10_PWM/SS, Part4.TXD
  N7: Part2.D11_PWM/MOSI, Part4.RXD
  N8: Part2.D0/RX, S2.L1
  N9: Part2.D1/TX, IC2.pin17
  N10: Part2.D2, IC2.pin1, IC2.pin19
  5V_2: Part2.5V, Part4.VCC, IC2.pin20, R2.Pin_0
  N11: IC1.pin2, IC1.pin3, R1.Pin_1, JP1.1
  N12: IC1.pin18, S1.L2
  N13: IC2.pin2, IC2.pin3, JP2.1, R2.Pin_1
  N14: IC2.pin18, S2.L2

notes:
  Master
  Slave
  9-12V
  Open to
  program Arduino
  To Dynamixel
  AX-12 Master
  AX-12 Slave
  The two circuits only share Vcc and Gnd.
  Gnd
